# Fritzing sketch mobile phone travel charger (saved by Fritzing 0.9.6b)
circuit board: 11.978cm x 6.21041cm
breadboards: 1

parts:
  R1 = Resistor [tolerance=±5% resistance=220 package="0402 [SMD]"]
  R2 = Resistor [tolerance=±5% resistance=220 package="0402 [SMD]"]
  R3 = Resistor [tolerance=±5% resistance=220 package="0805 [SMD]"]
  R4 = Resistor [tolerance=±5% resistance=220 package="0805 [SMD]"]
  R5 = Resistor [tolerance=±5% resistance=220 package="0402 [SMD]"]
  C1 = Capacitor [package=cap-pth-small-kit]
  D1 = Zener Diode [part_number=1N4732A breakdown_voltage=3.6V package="300 mil [THT]"]
  BAT1 = Battery Holders [package=battery-aa]
  Q1 = PNP-Transistor [package="TO92 [THT]"]
  Q2 = NPN-Transistor [package="TO92 [THT]"]
  S1 = Round Pushbutton
  LED1 = smd LED [color="Red (633nm)" package="0603 [SMD]"]

nets:
  N1: R1.Pin_0, C1.1, C1.2, D1.anode, BAT1.-, Q2.E, LED1.cathode, LED1.anode
  N2: R1.Pin_1, Q2.B
  N3: R2.Pin_0, R2.Pin_1, R3.Pin_0, Q1.E, Q2.C, S1.leg1
  N4: R3.Pin_1, Q1.B
  N5: R4.Pin_0, R5.Pin_0, Q1.C
  N6: R4.Pin_1, D1.cathode
  N7: BAT1.+, S1.leg0
